# Fritzing sketch FinalCircuit (saved by Fritzing 1.0.1rc)
breadboards: 1

parts:
  Pololu_A3 = Pololu A4988 [package=SO16]
  M3 = Stepper Motor - Bipolar
  S1 = Pushbutton [package=THT]
  R1 = Resistor [tolerance=±5% power=0.25W resistance=10000 package=THT]
  R2 = Resistor [tolerance=±5% power=0.25W resistance=10000 package=THT]
  S2 = Pushbutton [package=THT]
  R3 = Resistor [tolerance=±5% power=0.25W resistance=10000 package=THT]
  S3 = Pushbutton [package=THT]
  S4 = Toggle Switch [package=THT]
  S5 = Toggle Switch [package=THT]
  S6 = Toggle Switch [package=THT]
  S7 = Toggle Switch [package=THT]
  S8 = Toggle Switch [package=THT]
  S9 = Toggle Switch [package=THT]
  S10 = Toggle Switch [package=THT]
  S11 = Toggle Switch [package=THT]
  Part1 = Arduino Mega 2560 (Rev3)
  Pololu_A4 = Pololu A4988 [package=SO16]
  M4 = Stepper Motor - Bipolar
  Pololu_A5 = Pololu A4988 [package=SO16]
  M5 = Stepper Motor - Bipolar

nets:
  N1: Pololu_A3.STEP, Part1.D3_PWM
  N2: Pololu_A3.DIR, Part1.D7_PWM
  GND: Pololu_A3.GND, Pololu_A4.GND, Pololu_A5.GND
  N3: Pololu_A3.1B, M3.D
  N4: Pololu_A3.1A, M3.B
  N5: Pololu_A3.2A, M3.C
  N6: Pololu_A3.2B, M3.A
  N7: S1.leg1, R1.Pin_1
  N8: R1.Pin_0, R2.Pin_0, R3.Pin_0, S4.COM, S5.COM, S6.COM, S7.COM, S8.COM, S9.COM, S10.COM, S11.COM
  N9: R2.Pin_1, S2.leg1
  N10: R3.Pin_1, S3.leg1
  N11: Part1.D9_PWM, Pololu_A5.DIR
  N12: Part1.D8_PWM, Pololu_A4.DIR
  N13: Part1.D2_PWM, Pololu_A4.STEP
  N14: Part1.D4_PWM, Pololu_A5.STEP
  N15: Pololu_A4.1B, M4.D
  N16: Pololu_A4.1A, M4.B
  N17: Pololu_A4.2A, M4.C
  N18: Pololu_A4.2B, M4.A
  N19: Pololu_A5.2A, M5.C
  N20: Pololu_A5.2B, M5.A
